# Fritzing sketch armchair (saved by Fritzing 0.9.2b)

parts:
  Part1 = Arduino Uno (Rev3)
  Forward_Servo = Basic Servo
  Left/Right_Servo = Basic Servo
  Raspberry_Pi1 = Raspberry Pi 2  # not connected
  VCC1 = Battery  # not connected

nets:
  N1: Part1.D10_PWM/SS, Left/Right_Servo.pulse
  N2: Part1.D11_PWM/MOSI, Forward_Servo.pulse
  GND: Part1.GND, Left/Right_Servo.gnd
